# Fritzing sketch diagram (saved by Fritzing 0.9.4)
breadboards: 1

parts:
  J1 = STM32 Nucleo boards
  R1 = Resistor [tolerance=±5% resistance=330 package=THT]
  LED1 = LED - 5mm [color="Red (633nm)" package="5 mm [THT]"]
  Part1 = Bluetooth HC-05 Macho
  Part2 = BME280 Breakout

nets:
  N1: J1.PC8, LED1.anode
  3V3: J1.3v3, Part1.VCC, Part2.SDO/ADR, Part2.3.3V
  GND: J1.GND, R1.Pin_0, Part1.GND, Part2.GND
  N2: J1.PB8, Part2.SCK/SCL
  N3: J1.PA9, Part1.RXD
  N4: J1.PA10, Part1.TXD
  N5: J1.PB7, Part2.SDI/SDA
  N6: R1.Pin_1, LED1.cathode
